# Fritzing sketch Shéma (saved by Fritzing 0.8.7b)
breadboards: 1

parts:
  U1 = ESP8266 ESP-01 Upgraded WiFi Module [part_number=ESP8266]
  X1 = USB Connectors [package=usb-minib-nostop]
  S4 = Magnetic Door Switch [package=reed_switch_plastic]
  U2 = V_REG_LD1117VXX [package=78xxl]
  R1 = Resistor [tolerance=±5% resistance=10k package=THT]

nets:
  N1: U1.VCC, S4.1, U2.IN
  N2: U1.GPIO_0, S4.2, R1.Pin_1
  GND: U1.GND, X1.GND, U2.GND, R1.Pin_0
  N3: X1.VBUS, U2.OUT

notes:
  Interrupteur
  Convertisseur 5V vers 3.3V
  Prise Mini USB
  ESP 01S
  10KOhms

custom parts:
  ESP8266 ESP-01 Upgraded WiFi Module: Upgraded Version ESP-01,all Flash are upgraded to 1M byte.Also support Cloud service remote transmission.
